// Logisim project circuitoEquivalenteLogisim.circ as structural Verilog: 1 circuit, main circuit main
module main (
  input  sw2,
  input  sw4,
  input  sw3,
  input  sw1,
  output z
);

  wire z0_out, z1_out, z2_out, z3_out, z4_out;

  and z3 (z3_out, ~sw2, ~sw4);  // AND_Gate
  and z4 (z4_out, ~sw4, ~sw3);  // AND_Gate
  and z2 (z2_out, ~sw2, ~sw3);  // AND_Gate
  and z0 (z0_out, ~sw2, ~sw1);  // AND_Gate
  and z1 (z1_out, ~sw3, ~sw1);  // AND_Gate
  or z5 (z, z3_out, z4_out, z2_out, z0_out, z1_out);
endmodule
